# Fritzing sketch Hardware setup (saved by Fritzing 0.9.8b)

parts:
  MH-ET_LIVE_ESP32_DEVKIT1 = MH-ET LIVE ESP32 DEVKIT 38 pins
  HC-SR04_Sensor_1 = HC-SR04 Ultrasonic Distance Sensor
  LED1 = LED - 3mm [color="Red (633nm)" current=0.030 package="3 mm [THT]"]
  R1 = Resistor [tolerance=±5% resistance=220 package="0603 [SMD]"]
  S1 = Reed switch [package=THT]

nets:
  N1: MH-ET_LIVE_ESP32_DEVKIT1.IO14, HC-SR04_Sensor_1.ECHO
  N2: MH-ET_LIVE_ESP32_DEVKIT1.IO12, HC-SR04_Sensor_1.TRIG
  N3: MH-ET_LIVE_ESP32_DEVKIT1.GND#58, HC-SR04_Sensor_1.GND
  5V: MH-ET_LIVE_ESP32_DEVKIT1.5V, HC-SR04_Sensor_1.VCC
  N4: MH-ET_LIVE_ESP32_DEVKIT1.GND#64, S1.pin_1
  N5: MH-ET_LIVE_ESP32_DEVKIT1.IO23, S1.pin_2
  N6: MH-ET_LIVE_ESP32_DEVKIT1.IO21, R1.Pin_0
  N7: MH-ET_LIVE_ESP32_DEVKIT1.GND#70, LED1.cathode
  N8: LED1.anode, R1.Pin_1

custom parts:
  MH-ET LIVE ESP32 DEVKIT 38 pins: http://mh.nodebb.com/topic/2/mh-et-live-esp32-devkit
